# Fritzing sketch ESP8266-12 breakout (saved by Fritzing 0.9.2b)
circuit board: 4.15291cm x 4.49295cm

parts:
  U1 = ESP8266 WiFi Module [part_number=ESP8266]
  R2 = Resistor [tolerance=±5% resistance=10k package="1206 [SMD]"]
  R1 = Resistor [tolerance=±5% resistance=10k package="1206 [SMD]"]
  U2 = AMS1117 [package=sot223]
  S1 = Pushbutton [package="[SMD]"]  # not connected
  S2 = Pushbutton [package="[SMD]"]  # not connected
  S3 = SPST Switch [package=ayz0202]
  Power_plug1 = Power plug
  Q2 = Basic FET P-Channel [package="D2Pak [SMD]"]  # not connected
  Q3 = Basic FET P-Channel [package="D2Pak [SMD]"]  # not connected
  Q4 = Basic FET P-Channel [package="D2Pak [SMD]"]  # not connected
  J2 = Screw terminal - 2 pins [package=THT]  # not connected
  J3 = Screw terminal - 2 pins [package=THT]  # not connected
  C2 = Tantalum Capacitor [capacitance=10µF voltage=16V package="A 3216 [SMD, tantalum]"]
  C3 = Ceramic Capacitor [capacitance=100nF package="1206 [SMD, multilayer]"]

nets:
  N1: U1.VCC, R1.Pin_0, S3.P, C3.1
  N2: U1.GPIO_2, R2.Pin_0
  N3: U1.CH_PD, R1.Pin_1
  N4: U1.GND, R2.Pin_1, C3.0
  GND: U2.GND, Power_plug1.GND, C2.-
  N5: U2.VOUT, S3.O, C2.+
  VIN: U2.VIN, Power_plug1.VCC

custom parts:
  ESP8266 WiFi Module: Generic WiFi Module based on the ESP8266 with onboard PCB antenna and UART communications
  AMS1117: AMS1117 1A LDO voltage regulator
