# Fritzing sketch ESP8266-12 breakout_v0.1 (saved by Fritzing 0.9.2b)
circuit board: 4.15291cm x 4.7cm

parts:
  U1 = ESP8266 WiFi Module [part_number=ESP8266]
  R2 = Resistor [tolerance=±5% resistance=10k package="1206 [SMD]"]
  R1 = Resistor [tolerance=±5% resistance=10k package="1206 [SMD]"]
  U2 = AMS1117 [package=sot223]
  Power_plug1 = Power plug
  Q2-B = Basic FET P-Channel [package="D2Pak [SMD]"]
  Q3-R = Basic FET P-Channel [package="D2Pak [SMD]"]
  Q4-G = Basic FET P-Channel [package="D2Pak [SMD]"]
  J2 = Screw terminal - 2 pins [package=THT]
  J3 = Screw terminal - 2 pins [package=THT]
  C2 = Tantalum Capacitor [capacitance=10µF voltage=16V package="A 3216 [SMD, tantalum]"]
  S3 = SPST Switch [package=switch-spdt]
  LED1 = smd LED [color="Red (633nm)" package="1206 [SMD]"]
  R3 = Resistor [tolerance=±5% resistance=10k package="1206 [SMD]"]
  R4 = Resistor [tolerance=±5% resistance=10k package="1206 [SMD]"]
  R5 = Resistor [tolerance=±5% resistance=10k package="1206 [SMD]"]
  RST = Pushbutton [package="[THT]"]
  PRG = Pushbutton [package="[THT]"]
  C3 = Ceramic Capacitor [capacitance=100nF package="1206 [SMD, multilayer]"]
  R6 = Resistor [tolerance=±5% resistance=10k package="1206 [SMD]"]
  Prog_header = male pin header, 4 pins [form="♂ (male)"]

nets:
  N1: U1.RXD, Prog_header.pin1
  N2: U1.VCC, R1.Pin_0, S3.P, C3.0, Prog_header.pin4
  N3: U1.GPIO_0, PRG.Pin_3, PRG.Pin_4
  N4: U1.GPIO_2, LED1.anode
  N5: U1.CH_PD, R1.Pin_1
  GND: U1.GND, R2.Pin_1, U2.GND, Power_plug1.GND, Q2-B.Gate, Q3-R.Gate, Q4-G.Gate, C2.-, RST.Pin_3, RST.Pin_4, PRG.Pin_1, PRG.Pin_2, C3.1, R6.Pin_0, Prog_header.pin3
  N6: U1.TXD, Prog_header.pin2
  N7: U1.GPIO_15, R6.Pin_1
  N8: U1.GPIO_16, R3.Pin_1
  N9: U1.GPIO_14, R4.Pin_1
  N10: U1.GPIO_12, R5.Pin_1
  N11: U1.REST, RST.Pin_2
  N12: R2.Pin_0, LED1.cathode
  N13: U2.VOUT, C2.+, S3.O
  12V-VCC: Power_plug1.VCC, J2.pin1
  N14: Q2-B.drain, R3.Pin_0
  N15: Q2-B.source, J2.pin2
  N16: Q3-R.drain, R5.Pin_0
  N17: Q3-R.source, J3.pin2
  N18: Q4-G.drain, R4.Pin_0
  N19: Q4-G.source, J3.pin1

notes:
  GND
  RX
  TX
  3.3V

custom parts:
  ESP8266 WiFi Module: Generic WiFi Module based on the ESP8266 with onboard PCB antenna and UART communications
  AMS1117: AMS1117 1A LDO voltage regulator
