# Fritzing sketch ESP8266-12 breakout_v0.3a (saved by Fritzing 0.9.2b)
circuit board: 4.15291cm x 4.7cm

parts:
  U1 = ESP8266 WiFi Module [part_number=ESP8266]
  R2 = Resistor [tolerance=±5% resistance=680 part_number="INDICATOR LED" package="1206 [SMD]"]
  R1 = Resistor [tolerance=±5% resistance=10k part_number="PULLUP RESISTOR" package="1206 [SMD]"]
  U2 = AMS1117 [package=sot223]
  Power_plug1 = Power plug
  J2 = Screw terminal - 2 pins [package=THT]
  J3 = Screw terminal - 2 pins [package=THT]
  C1 = Tantalum Capacitor [capacitance=10µF voltage=16V package="A 3216 [SMD, tantalum]"]
  POWER = SPST Switch [package=switch-spdt]
  LED1 = smd LED [color="Red (633nm)" package="1206 [SMD]"]
  R3 = Resistor [tolerance=±5% resistance=10k part_number="B TRANS RESISTOR" package="1206 [SMD]"]
  R4 = Resistor [tolerance=±5% resistance=10k part_number="G TRANS RESISTOR" package="1206 [SMD]"]
  R5 = Resistor [tolerance=±5% resistance=10k part_number="R TRANS RESISTOR" package="1206 [SMD]"]
  RST = Pushbutton [package="[THT]"]
  PRG = Pushbutton [package="[THT]"]
  C2 = Ceramic Capacitor [capacitance=0.1µF part_number="DECOUPLING CAP" package="1206 [SMD, multilayer]"]
  R6 = Resistor [tolerance=±5% resistance=10k part_number="PULLDOWN RESISTOR" package="1206 [SMD]"]
  Prog_header = male pin header, 4 pins [form="♂ (male)"]
  GPIO = female pin header, 2 pins [form="♀ (female)" part_number="5       4"]
  Q1(R)1 = Basic FET P-Channel [package="D2Pak [SMD]"]  # not connected
  Q1(R)2 = Basic FET N-Channel [package="DPak [SMD]"]
  Q1(R)3 = Basic FET N-Channel [package="DPak [SMD]"]
  Q1(R)4 = Basic FET N-Channel [package="DPak [SMD]"]
  S1 = Pushbutton [package="[THT]"]  # not connected

nets:
  N1: U1.RXD, Prog_header.pin1
  N2: U1.VCC, R1.Pin_0, POWER.P, C2.0, Prog_header.pin4
  N3: U1.GPIO_0, PRG.Pin_3, PRG.Pin_4
  N4: U1.GPIO_2, LED1.anode
  N5: U1.CH_PD, R1.Pin_1
  GND: U1.GND, R2.Pin_1, U2.GND, Power_plug1.GND, C1.-, RST.Pin_3, RST.Pin_4, PRG.Pin_1, PRG.Pin_2, C2.1, R6.Pin_0, Prog_header.pin3, Q1(R)2.source, Q1(R)3.source, Q1(R)4.source
  N6: U1.TXD, Prog_header.pin2
  N7: U1.GPIO_15, R6.Pin_1
  N8: U1.GPIO_4, GPIO.pin1
  N9: U1.GPIO_5, GPIO.pin2
  N10: U1.GPIO_16, R3.Pin_1
  N11: U1.GPIO_14, R4.Pin_1
  N12: U1.GPIO_12, R5.Pin_1
  N13: U1.REST, RST.Pin_2
  N14: R2.Pin_0, LED1.cathode
  N15: U2.VOUT, C1.+, POWER.O
  12V-VCC: U2.VIN, Power_plug1.VCC, J2.pin1
  N16: J2.pin2, Q1(R)2.drain
  N17: J3.pin1, Q1(R)3.drain
  N18: J3.pin2, Q1(R)4.drain
  N19: R3.Pin_0, Q1(R)4.Gate
  N20: R4.Pin_0, Q1(R)3.Gate
  N21: R5.Pin_0, Q1(R)2.Gate

notes:
  GND
  RX
  TX
  3.3V
  +
  Designed By
  TinyStrip RGB LED
  Strip Controller
  v0.2
  Jeff Murchison
  murchlabs.com
  12VDC
  MAX
  B
  G
  R

custom parts:
  ESP8266 WiFi Module: Generic WiFi Module based on the ESP8266 with onboard PCB antenna and UART communications
  AMS1117: AMS1117 1A LDO voltage regulator
  Pushbutton: A generic pushbutton.
