# Fritzing sketch ESP8266-12 breakout_v0.4b (saved by Fritzing 0.9.2b)
circuit board: 4cm x 5cm

parts:
  U1 = ESP8266 WiFi Module [part_number=ESP8266]
  R2 = Resistor [tolerance=±5% resistance=680 part_number="INDICATOR LED" package="1206 [SMD]"]
  R1 = Resistor [tolerance=±5% resistance=10k part_number="PULLUP RESISTOR" package="1206 [SMD]"]
  U2 = AMS1117 [package=sot223]
  Power_plug1 = Power plug
  J2 = Screw terminal - 2 pins [package=THT]
  J3 = Screw terminal - 2 pins [package=THT]
  C1 = Tantalum Capacitor [capacitance=10µF voltage=16V package="A 3216 [SMD, tantalum]"]
  POWER = SPST Switch [package=switch-spdt]
  LED1 = smd LED [color="Red (633nm)" package="1206 [SMD]"]
  R3 = Resistor [tolerance=±5% resistance=10k part_number="B TRANS RESISTOR" package="1206 [SMD]"]
  R4 = Resistor [tolerance=±5% resistance=10k part_number="G TRANS RESISTOR" package="1206 [SMD]"]
  R5 = Resistor [tolerance=±5% resistance=10k part_number="R TRANS RESISTOR" package="1206 [SMD]"]
  C2 = Ceramic Capacitor [capacitance=0.1µF part_number="DECOUPLING CAP" package="1206 [SMD, multilayer]"]
  R6 = Resistor [tolerance=±5% resistance=10k part_number="PULLDOWN RESISTOR" package="1206 [SMD]"]
  Q1(G) = Basic FET N-Channel [package="DPak [SMD]"]
  Q1(R) = Basic FET N-Channel [package="DPak [SMD]"]
  Q1(B) = Basic FET N-Channel [package="DPak [SMD]"]
  RST = Pushbutton [package="[THT]"]
  PROG = Pushbutton [package="[THT]"]
  Prog_header = male pin header, 4 pins [form="♂ (male)"]
  J6 = double row female pin header, 20 pins [form="♀ (female)"]
  J4 = double row female pin header, 20 pins [form="♀ (female)"]
  J5 = female pin header, 10 pins [form="♀ (female)"]  # not connected
  J7 = double row female pin header, 14 pins [form="♀ (female)"]

nets:
  N1: U1.RXD, Prog_header.pin1
  N2: U1.VCC, R1.Pin_0, POWER.P, C2.0, Prog_header.pin4
  N3: U1.GPIO_0, PROG.Pin_2
  N4: U1.GPIO_2, LED1.anode, J6.pin10
  N5: U1.CH_PD, R1.Pin_1
  GND: U1.GND, R2.Pin_1, U2.GND, Power_plug1.GND, C1.-, C2.1, R6.Pin_0, Q1(G).source, Q1(R).source, Q1(B).source, RST.Pin_1, PROG.Pin_1, Prog_header.pin3, J6.pin11
  N6: U1.TXD, Prog_header.pin2
  N7: U1.GPIO_15, R6.Pin_1
  N8: U1.GPIO_4, J4.pin10
  N9: U1.GPIO_5, J4.pin11
  N10: U1.ADC_0, J7.pin8
  N11: U1.GPIO_16, R3.Pin_1
  N12: U1.GPIO_14, R4.Pin_1
  N13: U1.GPIO_12, R5.Pin_1
  N14: U1.GPIO_13, J7.pin9
  N15: U1.REST, RST.Pin_2
  N16: R2.Pin_0, LED1.cathode
  N17: U2.VOUT, C1.+, POWER.O
  12V-VCC: U2.VIN, Power_plug1.VCC, J2.pin1
  N18: J2.pin2, Q1(B).drain
  N19: J3.pin1, Q1(G).drain
  N20: J3.pin2, Q1(R).drain
  N21: R3.Pin_0, Q1(B).Gate
  N22: R4.Pin_0, Q1(R).Gate
  N23: R5.Pin_0, Q1(G).Gate

notes:
  GND
  RX
  TX
  3.3V
  +
  TinyStrip RGB LED
  Strip Controller v0.4
  12VDC
  MAX
  B
  G
  R
  Jeff Murchison
  Designed By
  murchlabs.com
  2
  5
  4
  ADC
  13

custom parts:
  ESP8266 WiFi Module: Generic WiFi Module based on the ESP8266 with onboard PCB antenna and UART communications
  AMS1117: AMS1117 1A LDO voltage regulator
  Pushbutton: A generic pushbutton.
