# Fritzing sketch ESP8266-12 breakout_v0.4d (saved by Fritzing 0.9.2b)
circuit board: 4cm x 5cm

parts:
  R1 = Resistor [tolerance=±5% resistance=10k part_number="PULLUP RESISTOR" package="1206 [SMD]"]
  VR1 = AMS1117 [package=sot223]
  Power_plug1 = Power plug
  J2 = Screw terminal - 2 pins [package=THT]
  J3 = Screw terminal - 2 pins [package=THT]
  C1 = Tantalum Capacitor [capacitance=10µF voltage=16V package="A 3216 [SMD, tantalum]"]
  POWER = SPST Switch [package=switch-spdt]
  R3 = Resistor [tolerance=±5% resistance=10k part_number="B TRANS RESISTOR" package="1206 [SMD]"]
  R4 = Resistor [tolerance=±5% resistance=10k part_number="G TRANS RESISTOR" package="1206 [SMD]"]
  R5 = Resistor [tolerance=±5% resistance=10k part_number="R TRANS RESISTOR" package="1206 [SMD]"]
  C2 = Ceramic Capacitor [capacitance=0.1µF part_number="DECOUPLING CAP" package="1206 [SMD, multilayer]"]
  R2 = Resistor [tolerance=±5% resistance=10k part_number="PULLDOWN RESISTOR" package="1206 [SMD]"]
  Q3(G) = Basic FET N-Channel [package="DPak [SMD]"]
  Q2(R) = Basic FET N-Channel [package="DPak [SMD]"]
  Q1(B) = Basic FET N-Channel [package="DPak [SMD]"]
  RST = Pushbutton [package="[THT]"]
  PROG = Pushbutton [package="[THT]"]
  Prog_header = male pin header, 4 pins [form="♂ (male)"]
  J7 = double row female pin header, 14 pins [form="♀ (female)"]
  J5 = female pin header, 9 pins [form="♀ (female)"]
  ESP-12F = ESP-12F (ESP8266 WiFi Module) [part_number=ESP8266]
  J9 = female pin header, 13 pins [form="♀ (female)"]
  J6 = double row female pin header, 26 pins [form="♀ (female)"]
  J10 = female pin header, 13 pins [form="♀ (female)"]

nets (from the pcb view):
  N1: R1.Pin_0, POWER.P, C2.0, Prog_header.pin4, ESP-12F.VCC, J9.pin13
  N2: R1.Pin_1, ESP-12F.EN
  GND: VR1.GND, Power_plug1.GND, C1.-, C2.1, R2.Pin_0, Q3(G).source, Q2(R).source, Q1(B).source, RST.Pin_1, PROG.Pin_1, Prog_header.pin3, ESP-12F.GND, J6.pin13
  N3: VR1.VOUT, C1.+, POWER.O
  VIN: VR1.VIN, Power_plug1.VCC, J2.pin1
  N4: J2.pin2, Q3(G).drain
  N5: J3.pin1, Q2(R).drain
  N6: J3.pin2, Q1(B).drain
  N7: R3.Pin_0, Q1(B).Gate
  N8: R3.Pin_1, ESP-12F.GPIO16
  N9: R4.Pin_0, Q2(R).Gate
  N10: R4.Pin_1, ESP-12F.GPIO14
  N11: R5.Pin_0, Q3(G).Gate
  N12: R5.Pin_1, ESP-12F.GPIO12
  N13: R2.Pin_1, ESP-12F.GPIO15
  N14: RST.Pin_2, ESP-12F.RST
  N15: PROG.Pin_2, ESP-12F.GPIO0
  N16: Prog_header.pin1, ESP-12F.RXD0
  N17: Prog_header.pin2, ESP-12F.TXD0
  N18: J7.pin7, ESP-12F.SCLK
  N19: J7.pin8, ESP-12F.MOSI
  N20: J7.pin9, ESP-12F.GPIO10
  N21: J7.pin10, ESP-12F.GPIO9
  N22: J7.pin11, ESP-12F.MISO
  N23: J7.pin12, ESP-12F.CS0
  N24: J7.pin13, ESP-12F.GPIO13
  N25: J7.pin14, ESP-12F.ADC0
  N26: J5.pin9, ESP-12F.GPIO2
  N27: ESP-12F.GPIO4, J10.pin13
  N28: ESP-12F.GPIO5, J6.pin14

notes:
  GND
  RX
  TX
  3.3V
  12VDC MAX
  Jeff Murchison
  Designed By
  murchlabs.com
  2
  5
  4
  10
  ON
  OFF
  9
  MI
  CS
  13
  ADC0
  MO
  SCLK
  TinyStrip RGB LED
  Strip Controller v0.4
  B
  R
  G
  +
  VCC
  Build 0.4d
  VR1 is Labeled wrong,
  VIN, VOUT, GND
  should be (clockwise from top):
  Prototyping Area
  For some reason the scematic caused it to have all these weird ratsnest lines to GND that I can't delete.

custom parts:
  AMS1117: AMS1117 1A LDO voltage regulator
  Pushbutton: A generic pushbutton.
  ESP-12F (ESP8266 WiFi Module): WiFi Module based on the ESP8266 with onboard PCB antenna and UART communications
